// Logisim project CatPettingUnit.circ as structural Verilog: 5 circuits, main circuit main
module main (
);

  wire clock_1_out, ram_clk, ram_we;
  wire [15:0] ram_addr, ram_data, ram_input, rom_addr, rom_data;

  Clock clock_1 (.out(clock_1_out));
  ROM #(.addrWidth(16), .dataWidth(16)) rom_1 (.addr(rom_addr), .data(rom_data));
  CPU cpu_1 (
    .rom_data(rom_data), .ram_data(ram_data), .clk(clock_1_out), .ram_clock(ram_clk), .rom_Addr(rom_addr),
    .ram_we(ram_we), .ram_input(ram_input), .ram_addr(ram_addr));
  RAM #(.addrWidth(16), .dataWidth(16), .enables("line")) ram_1 (
    .addr(ram_addr), .we(ram_we), .clk(ram_clk), .din(ram_input), .dout(ram_data));

  // Notes on the sheet:
  //   contents of rom_1 (hex, n*v repeats v):
  //   2400 283f 2c03 a480 c502 2481 e180
endmodule

module ALU (
  input  [15:0] X,
  input  [2:0] OPC,
  input  [15:0] Y,
  output [15:0] RESULT,
  output is_equal
);

  wire [15:0] ADD_O, adder_2_out, ADDI_O, NAND_O, subtractor_1_out;

  Multiplexer #(.select(3), .width(16)) multiplexer_1 (
    .in0(ADD_O), .in1(ADDI_O), .in2(NAND_O), .in4(ADDI_O), .in5(ADDI_O), .out(RESULT), .sel(OPC));  // open: in3, in6, in7
  Adder #(.width(16)) adder_1 (.a(X), .b(Y), .out(ADD_O));  // open: cin, cout
  assign NAND_O = ~(X & Y);  // NAND_Gate nand_1, 16 bits wide
  Comparator #(.width(16)) comparator_1 (.a(X), .b(Y), .eq(is_equal));  // open: gt, lt
  Adder #(.width(16)) adder_2 (.a(X), .b(Y), .out(adder_2_out));  // open: cin, cout
  Multiplexer #(.width(16)) multiplexer_2 (.in0(adder_2_out), .in1(subtractor_1_out), .out(ADDI_O), .sel(Y[15]));
  Subtractor #(.width(16)) subtractor_1 (.a(X), .b({1'b0, Y[14:0]}), .out(subtractor_1_out));  // open: bin, bout

  // Other names for the same wires on the sheet: isEqual = is_equal
endmodule

module REGISTERS (
  input  [2:0] reg1_out_sel,
  input  [2:0] reg2_out_sel,
  input  [2:0] reg_write_reg,
  input  [15:0] reg_write_data,
  input  write_enable,
  input  clock,
  output [15:0] reg1_out,
  output [15:0] reg2_out
);

  wire we_r1, we_r2, we_r3, we_r4, we_r5, we_r6, we_r7;
  wire [15:0] in_r1, in_r2, in_r3, in_r4, in_r5, in_r6, in_r7, out_r1, out_r2, out_r3, out_r4, out_r5,
       out_r6, out_r7;

  Register #(.width(16)) r0 ();  // open: D, en, clk, Q, clr
  Register #(.width(16)) r4 (.D(in_r4), .en(we_r4), .clk(clock), .Q(out_r4));  // open: clr
  Demultiplexer #(.enable("true"), .select(3), .width(16)) demultiplexer_1 (
    .out1(in_r1), .out2(in_r2), .out3(in_r3), .out4(in_r4), .out5(in_r5), .out6(in_r6), .out7(in_r7),
    .in(reg_write_data), .sel(reg_write_reg), .en(write_enable));  // open: out0
  Register #(.width(16)) r1 (.D(in_r1), .en(we_r1), .clk(clock), .Q(out_r1));  // open: clr
  Register #(.width(16)) r5 (.D(in_r5), .en(we_r5), .clk(clock), .Q(out_r5));  // open: clr
  Multiplexer #(.select(3), .width(16)) multiplexer_1 (
    .in0({16{1'b0}}), .in1(out_r1), .in2(out_r2), .in3(out_r3), .in4(out_r4), .in5(out_r5), .in6(out_r6),
    .in7(out_r7), .out(reg1_out), .sel(reg1_out_sel));
  Register #(.width(16)) r2 (.D(in_r2), .en(we_r2), .clk(clock), .Q(out_r2));  // open: clr
  Register #(.width(16)) r6 (.D(in_r6), .en(we_r6), .clk(clock), .Q(out_r6));  // open: clr
  Decoder #(.select(3)) decoder_1 (
    .out1(we_r1), .out2(we_r2), .out3(we_r3), .out4(we_r4), .out5(we_r5), .out6(we_r6), .out7(we_r7),
    .sel(reg_write_reg), .en(write_enable));  // open: out0
  Register #(.width(16)) r3 (.D(in_r3), .en(we_r3), .clk(clock), .Q(out_r3));  // open: clr
  Register #(.width(16)) r7 (.D(in_r7), .en(we_r7), .clk(clock), .Q(out_r7));  // open: clr
  Multiplexer #(.select(3), .width(16)) multiplexer_2 (
    .in0({16{1'b0}}), .in1(out_r1), .in2(out_r2), .in3(out_r3), .in4(out_r4), .in5(out_r5), .in6(out_r6),
    .in7(out_r7), .out(reg2_out), .sel(reg2_out_sel));

  // Other names for the same wires on the sheet: reg1[2:0] = reg1_out_sel; reg1_data[15:0] = reg1_out;
  //   reg2[2:0] = reg2_out_sel; reg2_data[15:0] = reg2_out; reg_write[2:0] = reg_write_reg; WE = write_enable
endmodule

module CPU (
  input  [15:0] rom_data,
  input  [15:0] ram_data,
  input  clk,
  output [15:0] rom_Addr,
  output ram_clock,
  output ram_we,
  output [15:0] ram_addr,
  output [15:0] ram_input
);

  wire alu_1_is_equal, and_3_out, d_ff_1_q, d_ff_1_qn, decoder_1_out0, multiplexer_3_out, multiplexer_4_out,
       or_1_out, or_2_out, pc_clk, pull_resistor_1_node, reg_clk_lw, reg_clk_sw;
  wire [2:0] multiplexer_2_out, regB, regC;
  wire [6:0] imm_s_6;
  wire [6:3] demultiplexer_1_out0;
  wire [9:0] imm_10;
  wire [14:6] undriven;
  wire [15:0] adder_1_out, alu_1_result, beq_addr, demultiplexer_3_out0, jalr, multiplexer_1_out,
       multiplexer_5_out, multiplexer_6_out, registers_1_reg2_out, subtractor_1_out, X, Y;

  D_Flip_Flop d_ff_1 (.D(d_ff_1_qn), .clk(clk), .Q(d_ff_1_q), .Qn(d_ff_1_qn), .preset(1'b0), .reset(1'b0));
  Demultiplexer #(.select(3), .tristate("true"), .width(10)) demultiplexer_1 (
    .out0({regB, demultiplexer_1_out0, regC}), .out1({regB, imm_s_6}),
    .out2({regB, demultiplexer_1_out0, regC}), .out3(imm_10), .out4({regB, imm_s_6}), .out5({regB, imm_s_6}),
    .out6({regB, imm_s_6}), .out7({regB, imm_s_6}), .in(rom_data[9:0]), .sel(rom_data[15:13]));
  // Digital_Oscilloscope #(.nState(4)) digital_oscilloscope_1: pin names not known; wires that end beside it: clk, ram_clock, pc_clk, reg_clk_lw, reg_clk_sw
  and and_1 (ram_clock, d_ff_1_q, clk);
  and and_2 (pc_clk, d_ff_1_qn, clk);
  nor nor_1 (reg_clk_lw, d_ff_1_q, clk, ram_clock);
  nor nor_2 (reg_clk_sw, d_ff_1_qn, clk, pc_clk);
  LedBar #(.matrixcols(16)) ledbar_1 (
    .led0(rom_data[15]), .led1(rom_data[14]), .led2(rom_data[13]), .led3(rom_data[12]), .led4(rom_data[11]),
    .led5(rom_data[10]), .led6(rom_data[9]), .led7(rom_data[8]), .led8(rom_data[7]), .led9(rom_data[6]),
    .led10(rom_data[5]), .led11(rom_data[4]), .led12(rom_data[3]), .led13(rom_data[2]), .led14(rom_data[1]),
    .led15(rom_data[0]));
  Decoder #(.enable("false"), .select(3), .tristate("true")) decoder_1 (
    .out0(decoder_1_out0), .out1(decoder_1_out0), .out2(decoder_1_out0), .out3(decoder_1_out0),
    .out4(decoder_1_out0), .out7(decoder_1_out0), .sel(rom_data[15:13]));  // open: out5, out6
  or or_1 (or_1_out, rom_data[13], alu_1_is_equal);
  Multiplexer #(.select(3), .width(16)) multiplexer_1 (
    .in6(beq_addr), .in7(X), .out(multiplexer_1_out), .sel(rom_data[15:13]));  // open: in0, in1, in2, in3, in4, in5
  Multiplexer #(.select(3), .width(3)) multiplexer_2 (
    .in0(regC), .in1(regC), .in2(regC), .in3(regC), .in4(regC), .in5(rom_data[12:10]), .in6(rom_data[12:10]),
    .in7(regC), .out(multiplexer_2_out), .sel(rom_data[15:13]));
  Multiplexer #(.select(3)) multiplexer_3 (
    .in0(reg_clk_sw), .in1(reg_clk_sw), .in2(reg_clk_sw), .in3(reg_clk_sw), .in4(reg_clk_sw),
    .in5(reg_clk_lw), .in6(reg_clk_sw), .in7(reg_clk_sw), .out(multiplexer_3_out), .sel(rom_data[15:13]));
  and and_3 (and_3_out, rom_data[15], rom_data[14], or_1_out);
  Multiplexer #(.select(3)) multiplexer_4 (
    .in0(pc_clk), .in1(pc_clk), .in2(pc_clk), .in3(pc_clk), .in4(pc_clk), .in5(pc_clk), .in6(pc_clk),
    .in7(reg_clk_sw), .out(multiplexer_4_out), .sel(rom_data[15:13]));
  Multiplexer #(.select(3), .width(16)) multiplexer_5 (
    .in0(alu_1_result), .in1(alu_1_result), .in2(alu_1_result), .in3({imm_10, {6{1'b0}}}), .in4(ram_data),
    .in7(jalr), .out(multiplexer_5_out), .sel(rom_data[15:13]));  // open: in5, in6
  Adder #(.width(16)) adder_1 (
    .a(jalr), .b({imm_s_6[6], {9{1'b0}}, imm_s_6[5:0]}), .out(adder_1_out));  // open: cin, cout
  Multiplexer #(.width(16)) multiplexer_6 (
    .in0(adder_1_out), .in1(subtractor_1_out), .out(multiplexer_6_out), .sel(imm_s_6[6]));
  Subtractor #(.width(16)) subtractor_1 (
    .a(jalr), .b({{10{1'b0}}, imm_s_6[5:0]}), .out(subtractor_1_out));  // open: bin, bout
  PC pc_1 (
    .WE(and_3_out), .pc_clk(multiplexer_4_out), .instuction_addr_set(multiplexer_1_out),
    .intruction_addr_out(rom_Addr));
  Multiplexer #(.width(16)) multiplexer_7 (.in1(multiplexer_6_out), .out(beq_addr), .sel(alu_1_is_equal));  // open: in0
  ALU alu_1 (.X(X), .OPC(rom_data[15:13]), .Y(Y), .RESULT(alu_1_result), .is_equal(alu_1_is_equal));
  REGISTERS registers_1 (
    .reg1_out_sel(regB), .reg2_out_sel(multiplexer_2_out), .reg_write_reg(rom_data[12:10]),
    .reg_write_data(multiplexer_5_out), .write_enable(decoder_1_out0), .clock(multiplexer_3_out),
    .reg1_out(X), .reg2_out(registers_1_reg2_out));
  Adder #(.width(16)) adder_2 (.a(rom_Addr), .b(16'h1), .out(jalr));  // open: cin, cout
  Multiplexer #(.select(3)) multiplexer_8 (
    .in0(1'b0), .in1(1'b0), .in2(1'b0), .in3(1'b0), .in4(1'b0), .in5(or_2_out), .in6(1'b0), .in7(1'b0),
    .out(ram_we), .sel(rom_data[15:13]));
  Demultiplexer #(.select(3), .tristate("true"), .width(16)) demultiplexer_2 (
    .out4(ram_addr), .out5(ram_addr), .in(alu_1_result), .sel(rom_data[15:13]));  // open: out0, out1, out2, out3, out6, out7
  Demultiplexer #(.select(3), .tristate("true"), .width(16)) demultiplexer_3 (
    .out0(demultiplexer_3_out0), .out1(demultiplexer_3_out0), .out2(demultiplexer_3_out0),
    .out3(demultiplexer_3_out0), .out4(demultiplexer_3_out0), .out5(ram_input), .out6(demultiplexer_3_out0),
    .out7(demultiplexer_3_out0), .in(registers_1_reg2_out), .sel(rom_data[15:13]));
  or or_2 (or_2_out, pc_clk, reg_clk_sw);
  Multiplexer #(.width(16)) multiplexer_9 (
    .in0(demultiplexer_3_out0), .in1({imm_s_6[6], undriven, imm_s_6[5:0]}), .out(Y),
    .sel(pull_resistor_1_node));
  Pull_Resistor pull_resistor_1 (.node(pull_resistor_1_node));
  Decoder #(.enable("false"), .select(3), .tristate("true")) decoder_2 (
    .out1(pull_resistor_1_node), .out4(pull_resistor_1_node), .out5(pull_resistor_1_node),
    .sel(rom_data[15:13]));  // open: out0, out2, out3, out6, out7

  // Other names for the same wires on the sheet: a_clk = ram_clock; instruction[15:0] = rom_data;
  //   regA[2:0] = rom_data[12:10]; opc[2:0] = rom_data[15:13]; lui[15:6] = imm_10
endmodule

module PC (
  input  WE,
  input  pc_clk,
  input  [15:0] instuction_addr_set,
  output [15:0] intruction_addr_out
);

  wire d_ff_1_q, d_ff_1_qn;

  D_Flip_Flop d_ff_1 (.D(d_ff_1_qn), .clk(pc_clk), .Q(d_ff_1_q), .Qn(d_ff_1_qn));  // open: preset, reset
  Counter #(.max('hffff), .width(16)) counter_1 (
    .load(WE), .count(1'b1), .clk(d_ff_1_q), .D(instuction_addr_set), .Q(intruction_addr_out));  // open: clr, up, carry
endmodule
